# Fritzing sketch ds18b20_reader (saved by Fritzing 0.9.3b)

parts:
  U2 = ESP8266 WiFi Module [part_number=ESP8266]
  R6 = Resistor [tolerance=±5% resistance=1k package=THT]
  R7 = Resistor [tolerance=±5% resistance=1k package=THT]
  R8_1-wire_pullup = Resistor [tolerance=±5% resistance=220 package=THT]
  DS1 = DS18B20 1-Wire Temperature Sensor [part_number=DS18B20]
  U3 = Voltage Regulator - 3.3V [package="TO220 [THT]"]
  VCC1 = 4 x AAA Battery Mount
  R8 = Resistor [tolerance=±5% resistance=120k package=THT]
  R9 = Resistor [tolerance=±5% resistance=39k package=THT]

nets:
  N1: U2.IO2, R6.Pin_1
  N2: U2.3.3V#10, R6.Pin_0, R7.Pin_0, R8_1-wire_pullup.Pin_0
  N3: U2.3.3V#11, DS1.VDD
  N4: U2.GND#12, DS1.GND
  N5: U2.GND#13, U2.IO15
  N6: U2.IO5, R8_1-wire_pullup.Pin_1, DS1.DQ
  N7: U2.T_OUT, R8.Pin_0, R9.Pin_0
  N8: U2.RST, U2.XPD
  N9: U2.CHIP_EN, R7.Pin_1
  N10: U2.GND#23, U3.GND, VCC1.-, R9.Pin_1
  N11: U2.3.3V#26, U3.output_voltage
  N12: U3.input_voltage, VCC1.+, R8.Pin_1

notes:
  1 piece 18650
  3.7 volts nominal
  voltage
  divider
